# Fritzing sketch two_diods (saved by Fritzing 0.8.3b)
breadboards: 1

parts:
  Part1 = Arduino Uno (Rev3)
  IR1 = TSOP312.., 314.. [package=THT]
  LED1 = LED - 5mm [color="Green (565nm)" package="5 mm [THT]"]
  LED2 = LED - 5mm [color="Yellow (592nm)" package="5 mm [THT]"]
  LED3 = LED - 5mm [color="Red (633nm)" package="5 mm [THT]"]

nets:
  N1: Part1.ICSP_SCK, Part1.D13/SCK, LED3.anode
  N2: Part1.ICSP_MOSI, Part1.D11_PWM/MOSI, IR1.GND
  N3: Part1.GND, IR1.Vs, LED1.cathode, LED2.cathode, LED3.cathode
  N4: Part1.D9_PWM, LED2.anode
  N5: Part1.D10_PWM/SS, LED1.anode
  N6: Part1.5V, IR1.Data
